# Fritzing sketch Sketch (saved by Fritzing 0.9.1b)
breadboards: 1

parts:
  Part1 = Arduino Uno (Rev3)
  J1 = Piezo Speaker
  LED1 = smd LED [color="Green (555nm)" package="0805 [SMD]"]
  LED2 = smd LED [color="Blue (430nm)" package="0805 [SMD]"]
  LED3 = smd LED [color="Orange (620nm)" package="0805 [SMD]"]
  LED4 = smd LED [color="Red (635nm)" package="0805 [SMD]"]
  R1 = Resistor [tolerance=±5% resistance=220 package=THT]
  R2 = Resistor [tolerance=±5% resistance=220 package=THT]
  R3 = Resistor [tolerance=±5% resistance=220 package=THT]
  part = Resistor [tolerance=±5% resistance=220 package=THT]
  R5 = Resistor [tolerance=±5% resistance=220 package=THT]
  U1 = RJ45 Jack [package=rj45-8]
  R6 = Resistor [tolerance=±5% resistance=10k package=THT]
  R7 = Resistor [tolerance=±5% resistance=10k package=THT]
  R8 = Resistor [tolerance=±5% resistance=10k package=THT]
  part_2 = Resistor [tolerance=±5% resistance=10k package=THT]

nets:
  N1: Part1.D9_PWM, J1.pin2
  N2: Part1.D10_PWM/SS, LED4.anode
  N3: Part1.D11_PWM/MOSI, LED2.anode
  N4: Part1.D12/MISO, LED1.anode
  N5: Part1.D13/SCK, LED3.anode
  N6: Part1.D0/RX, U1.5
  N7: Part1.D2, U1.6
  N8: Part1.D3_PWM, U1.3, R7.Pin_1
  N9: Part1.D4, U1.7
  N10: Part1.D5_PWM, U1.2, R8.Pin_1
  N11: Part1.D6_PWM, U1.8
  N12: Part1.D7, U1.1, R6.Pin_1
  N13: Part1.GND, R1.Pin_0, R2.Pin_0, R3.Pin_0, part.Pin_0, R5.Pin_0, R6.Pin_0, R7.Pin_0, R8.Pin_0, part_2.Pin_0
  N14: J1.pin1, R5.Pin_1
  N15: LED1.cathode, R3.Pin_1
  N16: LED2.cathode, R2.Pin_1
  N17: LED3.cathode, part.Pin_1
  N18: LED4.cathode, R1.Pin_1
  N19: U1.4, part_2.Pin_1

notes:
  This is the end of a rj-45 cable that has been cut in half.
  Adjust the size of this resistor to set the preferred volume of the piezo buzzer. 220Ω is a good starting point.
